# Fritzing sketch Sensor de Chuva (saved by Fritzing 0.9.4)

parts:
  YL-83_-_Control_Board2 = YL-83 Rain Sensor - Control Board
  YL-83_-_Detection_Board2 = YL-83 Rain Sensor - Detection Board
  U1 = ESP8266 NodeMCU LoLin module
  R1 = Resistor [tolerance=±5% resistance=3.3k package="2512 [SMD]"]
  S1 = Reed switch [package=THT]
  JP1 = Header 2 [package=screwterminal-3.5mm-2_lock]
  D1 = Diode [package=diode-1n4148]
  D2 = P1000K [part_number=1N4007]
  R2 = Resistor [tolerance=±5% resistance=1k package=THT]
  R3 = Resistor [tolerance=±5% resistance=10k package=THT]
  Q1 = NPN-Transistor [part_number=BC547 package="TO92 [THT]"]
  JP2 = Header 2 [package=screwterminal-3.5mm-2_lock]
  R4 = Resistor [tolerance=±5% resistance=1k package=THT]
  R5 = Resistor [tolerance=±5% resistance=1k package=THT]
  R6 = Resistor [tolerance=±5% resistance=1k package=THT]
  LED_WIFI = LED - 5mm [color="Green (555nm)" package="5 mm [THT]"]
  LED_CHUVA = LED - 5mm [color="Red (633nm)" package="5 mm [THT]"]
  LED_REED = LED - 5mm [color="Orange (605nm)" package="5 mm [THT]"]

nets:
  VCC: YL-83_-_Control_Board2.VCC, U1.3V3, R1.Pin_0
  GND: YL-83_-_Control_Board2.GND, U1.GND, S1.pin_2, JP1.1, R3.Pin_0, Q1.E, JP2.2, R4.Pin_0, R5.Pin_0, R6.Pin_0
  N1: YL-83_-_Control_Board2.DO, U1.D6
  N2: YL-83_-_Control_Board2.POS, YL-83_-_Detection_Board2.POS
  N3: YL-83_-_Control_Board2.NEG, YL-83_-_Detection_Board2.NEG
  N4: U1.D0, D2.anode
  N5: U1.D2, LED_WIFI.cathode
  N6: U1.D3, LED_CHUVA.cathode
  N7: U1.D5, LED_REED.cathode
  N8: U1.D7, R1.Pin_1, S1.pin_1
  N9: U1.Vin, D1.C
  N10: JP1.2, D1.A
  N11: D2.cathode, R2.Pin_1
  N12: R2.Pin_0, R3.Pin_1, Q1.B
  N13: Q1.C, JP2.1
  N14: R4.Pin_1, LED_REED.anode
  N15: R5.Pin_1, LED_WIFI.anode
  N16: R6.Pin_1, LED_CHUVA.anode

custom parts:
  YL-83 Rain Sensor - Control Board: The YL-83 is a rain sensor that has more resistance when dry and less resistance when wet. The module runs at 5V.
  YL-83 Rain Sensor - Detection Board: The YL-83 is a rain sensor that has more resistance when dry and less resistance when wet. The module runs at 5V.
  ESP8266 NodeMCU LoLin module: ESP8266 based NodeMCU
